# Fritzing sketch Plane Launcher Schematic (saved by Fritzing 0.9.4)
breadboards: 1

parts:
  Raspberry_Pi = Raspberry Pi B+
  Catapult = Basic Servo [part_number=sg90]

nets:
  N1: Raspberry_Pi.GPIO22, Catapult.pulse
  GND: Raspberry_Pi.GND, Catapult.gnd
  5V: Raspberry_Pi.5V, Catapult.vcc
